// Logisim project flipflop.circ as structural Verilog: 4 circuits, main circuit ffd
module latch (
  input  in_1,
  input  in_2,
  output out_3,
  output out_4
);

  or or_1 (out_3, ~in_1, ~out_4);  // OR_Gate
  or or_2 (out_4, ~out_3, ~in_2);  // OR_Gate
endmodule

module ffsr (
  input  S,
  input  CLK,
  input  R,
  output out_4,
  output out_5
);

  wire nand_1_out, nand_2_out;

  nand nand_1 (nand_1_out, S, CLK);
  nand nand_2 (nand_2_out, CLK, R);
  latch latch_1 (.in_1(nand_1_out), .in_2(nand_2_out), .out_3(out_4), .out_4(out_5));
endmodule

module ffjk (
  input  J,
  input  CLK,
  input  K,
  output out_4,
  output out_5
);

  wire nand_1_out, nand_2_out;

  nand nand_1 (nand_1_out, out_5, J, CLK);
  latch latch_1 (.in_1(nand_1_out), .in_2(nand_2_out), .out_3(out_4), .out_4(out_5));
  nand nand_2 (nand_2_out, CLK, K, out_4);
endmodule

module ffd (
  input  D,
  input  CLK,
  output out_3,
  output out_4
);

  wire not_1_out;

  not not_1 (not_1_out, D);
  ffsr ffsr_1 (.S(D), .CLK(CLK), .R(not_1_out), .out_4(out_3), .out_5(out_4));
endmodule
