// Logisim project mat.circ as structural Verilog: 6 circuits, main circuit add1
module add1 (
  input  in_1,
  input  in_2,
  output out_3,
  output out_4
);

  xor xor_1 (out_3, in_1, in_2);
  and and_1 (out_4, in_2, in_1);
endmodule

module add1c (
  input  Ci,
  input  in_2,
  input  in_3,
  output out_4,
  output Co
);

  wire and_1_out, and_2_out, and_3_out, or_2_out, xor_1_out;

  xor xor_1 (xor_1_out, Ci, in_3);
  and and_1 (and_1_out, in_3, in_2);
  and and_2 (and_2_out, in_3, Ci);
  and and_3 (and_3_out, in_2, Ci);
  xor xor_2 (out_4, xor_1_out, in_2);
  or or_1 (Co, and_1_out, or_2_out);
  or or_2 (or_2_out, and_2_out, and_3_out);
endmodule

module add2c (
  input  Ci,
  input  Al,
  input  Ah,
  input  Bl,
  input  Bh,
  output out_6,
  output out_7,
  output Co
);

  wire add1c_1_co;

  add1c add1c_1 (.Ci(Ci), .in_2(Al), .in_3(Bl), .out_4(out_6), .Co(add1c_1_co));
  add1c add1c_2 (.Ci(add1c_1_co), .in_2(Ah), .in_3(Bh), .out_4(out_7), .Co(Co));
endmodule

module add4c (
  input  Ci,
  input  Al,
  input  in_3,
  input  in_4,
  input  Ah,
  input  Bl,
  input  in_7,
  input  in_8,
  input  Bh,
  output out_10,
  output out_11,
  output out_12,
  output out_13,
  output Co
);

  wire add2c_1_co;

  add2c add2c_1 (.Ci(Ci), .Al(Al), .Ah(in_3), .Bl(Bl), .Bh(in_7), .out_6(out_10), .out_7(out_11), .Co(add2c_1_co));
  add2c add2c_2 (.Ci(add2c_1_co), .Al(in_4), .Ah(Ah), .Bl(in_8), .Bh(Bh), .out_6(out_12), .out_7(out_13), .Co(Co));
endmodule

module add8c (
  input  in_1,
  input  in_2,
  input  in_3,
  input  in_4,
  input  in_5,
  input  in_6,
  input  in_7,
  input  in_8,
  input  in_9,
  input  in_10,
  input  in_11,
  input  in_12,
  input  in_13,
  input  in_14,
  input  in_15,
  input  in_16,
  input  in_17,
  output out_18,
  output out_19,
  output out_20,
  output out_21,
  output out_22,
  output out_23,
  output out_24,
  output out_25,
  output out_26
);

  wire add4c_1_co;

  add4c add4c_1 (
    .Ci(in_1), .Al(in_2), .in_3(in_3), .in_4(in_4), .Ah(in_5), .Bl(in_10), .in_7(in_11), .in_8(in_12),
    .Bh(in_13), .out_10(out_18), .out_11(out_19), .out_12(out_20), .out_13(out_21), .Co(add4c_1_co));
  add4c add4c_2 (
    .Ci(add4c_1_co), .Al(in_6), .in_3(in_7), .in_4(in_8), .Ah(in_9), .Bl(in_14), .in_7(in_15), .in_8(in_16),
    .Bh(in_17), .out_10(out_22), .out_11(out_23), .out_12(out_24), .out_13(out_25), .Co(out_26));
endmodule

module add8cs (
  input  Ci,
  input  [7:0] A,
  input  [7:0] B,
  output [7:0] out_4,
  output Co
);

  add8c add8c_1 (
    .in_1(Ci), .in_2(A[0]), .in_3(A[1]), .in_4(A[2]), .in_5(A[3]), .in_6(A[4]), .in_7(A[5]), .in_8(A[6]),
    .in_9(A[7]), .in_10(B[0]), .in_11(B[1]), .in_12(B[2]), .in_13(B[3]), .in_14(B[4]), .in_15(B[5]),
    .in_16(B[6]), .in_17(B[7]), .out_18(out_4[0]), .out_19(out_4[1]), .out_20(out_4[2]), .out_21(out_4[3]),
    .out_22(out_4[4]), .out_23(out_4[5]), .out_24(out_4[6]), .out_25(out_4[7]), .out_26(Co));
endmodule
