// Logisim project multiplex.circ as structural Verilog: 2 circuits, main circuit mplex2
module mplex1 (
  input  in_1,
  input  in_2,
  input  SLK,
  output out_4
);

  wire and_1_out, and_2_out;

  and and_1 (and_1_out, in_1, ~SLK);  // AND_Gate
  and and_2 (and_2_out, in_2, SLK);
  or or_1 (out_4, and_1_out, and_2_out);
endmodule

module mplex2 (
  input  in_1,
  input  in_2,
  input  in_3,
  input  in_4,
  input  SL,
  input  SH,
  output out_7
);

  wire mplex1_1_out_4, mplex1_2_out_4;

  mplex1 mplex1_1 (.in_1(in_1), .in_2(in_2), .SLK(SL), .out_4(mplex1_1_out_4));
  mplex1 mplex1_2 (.in_1(in_3), .in_2(in_4), .SLK(SL), .out_4(mplex1_2_out_4));
  mplex1 mplex1_3 (.in_1(mplex1_1_out_4), .in_2(mplex1_2_out_4), .SLK(SH), .out_4(out_7));
endmodule
